// Logisim project somador_subtrator_completo.circ as structural Verilog: 5 circuits, main circuit main
module main (
  input  A1,
  input  B1,
  input  C1,
  input  D1,
  input  M,
  input  A2,
  input  B2,
  input  C2,
  input  D2
);

  wire display_hexadecimal_1_1_a_2, display_hexadecimal_1_1_b_2, display_hexadecimal_1_1_c_2,
       display_hexadecimal_1_1_d_2, display_hexadecimal_1_1_e, display_hexadecimal_1_1_f,
       display_hexadecimal_1_1_g, display_hexadecimal_1_2_a_2, display_hexadecimal_1_2_b_2,
       display_hexadecimal_1_2_c_2, display_hexadecimal_1_2_d_2, display_hexadecimal_1_2_e,
       display_hexadecimal_1_2_f, display_hexadecimal_1_2_g, display_hexadecimal_1_3_a_2,
       display_hexadecimal_1_3_b_2, display_hexadecimal_1_3_c_2, display_hexadecimal_1_3_d_2,
       display_hexadecimal_1_3_e, display_hexadecimal_1_3_f, display_hexadecimal_1_3_g,
       display_hexadecimal_2_1_a_2, display_hexadecimal_2_1_b, display_hexadecimal_2_1_c,
       display_hexadecimal_2_1_d, display_hexadecimal_2_1_e, display_hexadecimal_2_1_f,
       display_hexadecimal_2_1_g, somador_subtrator_conjunto_1_s1, somador_subtrator_conjunto_1_s2,
       somador_subtrator_conjunto_1_s3, somador_subtrator_conjunto_1_s4, somador_subtrator_conjunto_1_ts;

  display_hexadecimal_1 display_hexadecimal_1_1 (
    .A(A1), .B(B1), .C(C1), .D(D1), .a_2(display_hexadecimal_1_1_a_2), .b_2(display_hexadecimal_1_1_b_2),
    .c_2(display_hexadecimal_1_1_c_2), .d_2(display_hexadecimal_1_1_d_2), .e(display_hexadecimal_1_1_e),
    .f(display_hexadecimal_1_1_f), .g(display_hexadecimal_1_1_g));
  _7_Segment_Display u_7_segment_display_1 (
    .g(display_hexadecimal_1_1_g), .f(display_hexadecimal_1_1_f), .a(display_hexadecimal_1_1_a_2),
    .b(display_hexadecimal_1_1_b_2), .e(display_hexadecimal_1_1_e), .d(display_hexadecimal_1_1_d_2),
    .c(display_hexadecimal_1_1_c_2));  // open: dp
  display_hexadecimal_2 display_hexadecimal_2_1 (
    .A(somador_subtrator_conjunto_1_ts), .a_2(display_hexadecimal_2_1_a_2), .b(display_hexadecimal_2_1_b),
    .c(display_hexadecimal_2_1_c), .d(display_hexadecimal_2_1_d), .e(display_hexadecimal_2_1_e),
    .f(display_hexadecimal_2_1_f), .g(display_hexadecimal_2_1_g));
  somador_subtrator_conjunto somador_subtrator_conjunto_1 (
    .A1(A1), .B1(B1), .C1(C1), .D1(D1), .M(M), .A2(A2), .B2(B2), .C2(C2), .D2(D2),
    .Ts(somador_subtrator_conjunto_1_ts), .S1(somador_subtrator_conjunto_1_s1),
    .S2(somador_subtrator_conjunto_1_s2), .S3(somador_subtrator_conjunto_1_s3),
    .S4(somador_subtrator_conjunto_1_s4));
  _7_Segment_Display u_7_segment_display_2 (
    .g(display_hexadecimal_2_1_g), .f(display_hexadecimal_2_1_f), .a(display_hexadecimal_2_1_a_2),
    .b(display_hexadecimal_2_1_b), .e(display_hexadecimal_2_1_e), .d(display_hexadecimal_2_1_d),
    .c(display_hexadecimal_2_1_c));  // open: dp
  display_hexadecimal_1 display_hexadecimal_1_2 (
    .A(somador_subtrator_conjunto_1_s1), .B(somador_subtrator_conjunto_1_s2),
    .C(somador_subtrator_conjunto_1_s3), .D(somador_subtrator_conjunto_1_s4),
    .a_2(display_hexadecimal_1_2_a_2), .b_2(display_hexadecimal_1_2_b_2), .c_2(display_hexadecimal_1_2_c_2),
    .d_2(display_hexadecimal_1_2_d_2), .e(display_hexadecimal_1_2_e), .f(display_hexadecimal_1_2_f),
    .g(display_hexadecimal_1_2_g));
  _7_Segment_Display u_7_segment_display_3 (
    .g(display_hexadecimal_1_2_g), .f(display_hexadecimal_1_2_f), .a(display_hexadecimal_1_2_a_2),
    .b(display_hexadecimal_1_2_b_2), .e(display_hexadecimal_1_2_e), .d(display_hexadecimal_1_2_d_2),
    .c(display_hexadecimal_1_2_c_2));  // open: dp
  display_hexadecimal_1 display_hexadecimal_1_3 (
    .A(A2), .B(B2), .C(C2), .D(D2), .a_2(display_hexadecimal_1_3_a_2), .b_2(display_hexadecimal_1_3_b_2),
    .c_2(display_hexadecimal_1_3_c_2), .d_2(display_hexadecimal_1_3_d_2), .e(display_hexadecimal_1_3_e),
    .f(display_hexadecimal_1_3_f), .g(display_hexadecimal_1_3_g));
  _7_Segment_Display u_7_segment_display_4 (
    .g(display_hexadecimal_1_3_g), .f(display_hexadecimal_1_3_f), .a(display_hexadecimal_1_3_a_2),
    .b(display_hexadecimal_1_3_b_2), .e(display_hexadecimal_1_3_e), .d(display_hexadecimal_1_3_d_2),
    .c(display_hexadecimal_1_3_c_2));  // open: dp
endmodule

module display_hexadecimal_2 (
  input  A,
  output a_2,
  output b,
  output c,
  output d,
  output e,
  output f,
  output g
);

  wire not_1_out, not_2_out, not_3_out, not_4_out, not_5_out;

  not not_1 (not_1_out, A);
  not not_2 (not_2_out, A);
  not not_3 (not_3_out, A);
  not not_4 (not_4_out, A);
  not not_5 (not_5_out, A);
  and and_1 (a_2, not_1_out, A);
  and and_2 (d, not_2_out, A);
  and and_3 (e, not_3_out, A);
  and and_4 (f, not_4_out, A);
  and and_5 (g, not_5_out, not_5_out, A);

  assign b = A;
  assign c = A;
endmodule

module somador_subtrator_completo (
  input  M,
  input  A,
  input  B,
  input  Te,
  output S,
  output Ts
);

  wire and_1_out, and_2_out, or_2_out, xor_1_out, xor_2_out;

  and and_1 (and_1_out, B, Te);
  xor xor_1 (xor_1_out, M, A);
  or or_1 (Ts, and_1_out, and_2_out);
  or or_2 (or_2_out, Te, B);
  and and_2 (and_2_out, xor_1_out, or_2_out);
  xor xor_2 (xor_2_out, A, B);
  xor xor_3 (S, xor_2_out, Te);
endmodule

module display_hexadecimal_1 (
  input  A,
  input  B,
  input  C,
  input  D,
  output a_2,
  output b_2,
  output c_2,
  output d_2,
  output e,
  output f,
  output g
);

  wire and_1_out, and_2_out, and_3_out, and_4_out, and_5_out, and_6_out, and_7_out, and_8_out, and_9_out,
       and_10_out, and_11_out, and_12_out, and_13_out, and_14_out, and_15_out, and_16_out, and_17_out,
       and_18_out, and_19_out, and_20_out, and_21_out, and_22_out, and_23_out, and_24_out, and_25_out,
       and_26_out, and_27_out, and_28_out, and_29_out, and_30_out, and_31_out, and_32_out, and_33_out,
       and_34_out, and_35_out, and_36_out, and_37_out, and_38_out, not_1_out, not_2_out, not_3_out,
       not_4_out, or_1_out, or_2_out, or_3_out, or_4_out, or_5_out, or_10_out;

  not not_1 (not_1_out, A);
  not not_2 (not_2_out, B);
  not not_3 (not_3_out, C);
  not not_4 (not_4_out, D);
  and and_1 (and_1_out, B, C);
  and and_2 (and_2_out, not_1_out, C);
  and and_3 (and_3_out, not_2_out, not_4_out);
  and and_4 (and_4_out, A, not_4_out);
  and and_5 (and_5_out, A, not_2_out, not_3_out);
  and and_6 (and_6_out, not_1_out, B, D);
  and and_7 (and_7_out, not_1_out, not_2_out);
  and and_8 (and_8_out, not_2_out, not_3_out);
  and and_9 (and_9_out, not_2_out, not_4_out);
  and and_10 (and_10_out, not_1_out, not_3_out, not_4_out);
  and and_11 (and_11_out, not_1_out, C, D);
  and and_12 (and_12_out, A, not_3_out, D);
  and and_13 (and_13_out, A, not_2_out);
  and and_14 (and_14_out, not_2_out, not_3_out);
  and and_15 (and_15_out, not_1_out, B);
  and and_16 (and_16_out, not_3_out, D);
  and and_17 (and_17_out, not_2_out, D);
  and and_18 (and_18_out, A, A, not_3_out);
  and and_19 (and_19_out, B, C, not_4_out);
  and and_20 (and_20_out, not_1_out, not_2_out, not_2_out, not_4_out);
  and and_21 (and_21_out, not_2_out, C, D);
  and and_22 (and_22_out, B, not_3_out, D);
  and and_23 (and_23_out, C, not_4_out);
  and and_24 (and_24_out, A, C);
  and and_25 (and_25_out, A, not_4_out);
  and and_26 (and_26_out, A, B);
  and and_27 (and_27_out, not_2_out, not_4_out);
  and and_28 (and_28_out, A, not_2_out);
  and and_29 (and_29_out, not_3_out, not_4_out);
  and and_30 (and_30_out, B, not_4_out);
  and and_31 (and_31_out, A, C);
  and and_32 (and_32_out, not_1_out, B, not_3_out);
  and and_33 (and_33_out, not_2_out, C);
  and and_34 (and_34_out, A, C);
  and and_35 (and_35_out, A, D);
  and and_36 (and_36_out, C, not_4_out);
  and and_37 (and_37_out, not_1_out, B, not_3_out);
  and and_38 (and_38_out, A, not_2_out, not_3_out);
  or or_1 (or_1_out, and_36_out, and_37_out, and_38_out);
  or or_2 (or_2_out, and_1_out, and_2_out, and_3_out);
  or or_3 (or_3_out, and_4_out, and_5_out, and_6_out);
  or or_4 (or_4_out, and_7_out, and_8_out, and_9_out);
  or or_5 (or_5_out, and_10_out, and_11_out, and_12_out);
  or or_6 (c_2, and_13_out, and_14_out, and_15_out, and_16_out, and_17_out);
  or or_7 (d_2, and_18_out, and_19_out, and_20_out, and_21_out, and_22_out);
  or or_8 (e, and_23_out, and_24_out, and_25_out, and_26_out, and_27_out);
  or or_9 (f, and_28_out, and_29_out, and_30_out, and_31_out, and_32_out);
  or or_10 (or_10_out, and_33_out, and_34_out, and_35_out);
  or or_11 (a_2, or_2_out, or_3_out);
  or or_12 (b_2, or_4_out, or_5_out);
  or or_13 (g, or_10_out, or_1_out);
endmodule

module somador_subtrator_conjunto (
  input  A1,
  input  B1,
  input  C1,
  input  D1,
  input  M,
  input  A2,
  input  B2,
  input  C2,
  input  D2,
  output Ts,
  output S1,
  output S2,
  output S3,
  output S4
);

  wire somador_subtrator_completo_2_ts, somador_subtrator_completo_3_ts, somador_subtrator_completo_4_ts;

  somador_subtrator_completo somador_subtrator_completo_1 (
    .M(M), .A(A1), .B(A2), .Te(somador_subtrator_completo_2_ts), .Ts(Ts), .S(S1));
  somador_subtrator_completo somador_subtrator_completo_2 (
    .M(M), .A(B1), .B(B2), .Te(somador_subtrator_completo_3_ts), .Ts(somador_subtrator_completo_2_ts), .S(S2));
  somador_subtrator_completo somador_subtrator_completo_3 (
    .M(M), .A(C1), .B(C2), .Te(somador_subtrator_completo_4_ts), .Ts(somador_subtrator_completo_3_ts), .S(S3));
  somador_subtrator_completo somador_subtrator_completo_4 (
    .M(M), .A(D1), .B(D2), .Te(1'b0), .Ts(somador_subtrator_completo_4_ts), .S(S4));
endmodule
